// Logisim project pr01.circ as structural Verilog: 3 circuits, main circuit nand_cmos
module nand_cmos (
  input  A,
  input  B,
  output Y
);

  wire transistor_3_out;

  Transistor #(.\type ("p")) transistor_1 (.in(1'b1), .out(Y), .gate(A));
  Transistor #(.\type ("n")) transistor_2 (.in(transistor_3_out), .out(Y), .gate(A));
  Transistor #(.\type ("n")) transistor_3 (.in(1'b0), .out(transistor_3_out), .gate(B));
  Transistor #(.\type ("p")) transistor_4 (.in(1'b1), .out(Y), .gate(B));

  // Notes on the sheet:
  //   VT1
  //   VT3
  //   VT4
  //   КМОП-элемент И-НЕ (NAND)
  //   VT2
endmodule

module F_sdnf (
  input  a,
  input  b,
  input  c,
  input  d,
  output F
);

  wire and_1_out, and_2_out, and_3_out, and_4_out, and_5_out, and_6_out, and_7_out, and_8_out, not_1_out,
       not_2_out, not_3_out, not_4_out;

  not not_1 (not_1_out, a);
  not not_2 (not_2_out, b);
  not not_3 (not_3_out, c);
  not not_4 (not_4_out, d);
  and and_1 (and_1_out, not_1_out, not_2_out, not_3_out, d);
  and and_2 (and_2_out, not_1_out, not_2_out, c, d);
  and and_3 (and_3_out, not_1_out, b, not_3_out, d);
  and and_4 (and_4_out, not_1_out, b, c, d);
  and and_5 (and_5_out, a, not_2_out, not_3_out, not_4_out);
  and and_6 (and_6_out, a, not_2_out, c, not_4_out);
  and and_7 (and_7_out, a, b, not_3_out, not_4_out);
  and and_8 (and_8_out, a, b, c, not_4_out);
  or or_1 (F, and_1_out, and_2_out, and_3_out, and_4_out, and_5_out, and_6_out, and_7_out, and_8_out);

  // Notes on the sheet:
  //   F = 55AA: схема по СДНФ (8 конституент единицы)
  //   m1
  //   m3
  //   m5
  //   m7
  //   m8
  //   m10
  //   m12
  //   m14
endmodule

module F_mknf (
  input  a,
  input  b,
  input  c,
  input  d,
  output F
);

  wire not_1_out, not_2_out, or_1_out, or_2_out;

  not not_1 (not_1_out, a);
  not not_2 (not_2_out, d);
  or or_1 (or_1_out, a, d);
  or or_2 (or_2_out, not_1_out, not_2_out);
  and and_1 (F, or_1_out, or_2_out);

  // Notes on the sheet:
  //   входы b и c в МКНФ не входят (функция от них не зависит)
  //   F = 55AA: схема по МКНФ  F = (a ∨ d)(¬a ∨ ¬d)
endmodule
