// Logisim project coder.circ as structural Verilog: 2 circuits, main circuit coder_4_2
module coder_4_2 (
  input  I0,
  input  I1,
  input  I2,
  input  I3,
  output a0,
  output a1
);

  or or_1 (a0, I1, I3);
  or or_2 (a1, I2, I3);

  // Notes on the sheet:
  //   Шифратор 4→2 (неприоритетный)
  //   I0 → код 00 (не подключается)
endmodule

module coder_4_2_prio (
  input  I0,
  input  I1,
  input  I2,
  input  I3,
  output a0,
  output a1
);

  wire and_1_out, not_1_out;

  not not_1 (not_1_out, I2);
  and and_1 (and_1_out, I1, not_1_out);
  or or_1 (a0, and_1_out, I3);
  or or_2 (a1, I2, I3);

  // Notes on the sheet:
  //   Шифратор 4→2 (приоритетный)
endmodule
