// Logisim project t_trigger.circ as structural Verilog: 1 circuit, main circuit t_trigger
module t_trigger (
  input  nS,
  input  nR,
  input  T,
  output Q,
  output nQ
);

  wire nand_1_out, nand_2_out, nand_4_out, nand_5_out, nand_6_out, nand_7_out, nT;

  nand nand_1 (nand_1_out, nQ, T);
  nand nand_2 (nand_2_out, T, Q);
  nand nand_3 (nT, T, T);
  nand nand_4 (nand_4_out, nS, nand_1_out, nand_5_out);
  nand nand_5 (nand_5_out, nand_4_out, nand_2_out, nR);
  nand nand_6 (nand_6_out, nand_4_out, nT);
  nand nand_7 (nand_7_out, nT, nand_5_out);
  nand nand_8 (Q, nS, nand_6_out, nQ);
  nand nand_9 (nQ, Q, nand_7_out, nR);

  // Notes on the sheet:
  //   G1
  //   G2
  //   G9
  //   ведущая ступень
  //   G3
  //   G4
  //   Асинхронный двухступенчатый T-триггер на элементах И-НЕ
  //   G5
  //   G6
  //   ведомая ступень
  //   G7
  //   G8
endmodule
