// Logisim project pr05_tlb.circ as structural Verilog: 1 circuit, main circuit TLB
module TLB (
  input  [19:0] VA,
  output HIT,
  output Page_Fault,
  output [6:0] VPN,
  output [12:0] Offset,
  output [7:0] PFN,
  output [20:0] PA
);

  wire EQ0, EQ1, EQ2, EQ3, H0, H1, H2, H3;
  wire [1:0] IDX;

  // Probe on VA
  Comparator #(.width(7), .mode("unsigned")) comparator_1 (.a(VA[19:13]), .b(7'b0001011), .eq(EQ0));  // open: gt, lt
  Comparator #(.width(7), .mode("unsigned")) comparator_2 (.a(VA[19:13]), .b({7{1'b0}}), .eq(EQ1));  // open: gt, lt
  Comparator #(.width(7), .mode("unsigned")) comparator_3 (.a(VA[19:13]), .b({7{1'b0}}), .eq(EQ2));  // open: gt, lt
  Comparator #(.width(7), .mode("unsigned")) comparator_4 (.a(VA[19:13]), .b({7{1'b0}}), .eq(EQ3));  // open: gt, lt
  and and_1 (H0, EQ0, 1'b1);
  and and_2 (H1, EQ1, 1'b0);
  and and_3 (H2, EQ2, 1'b0);
  and and_4 (H3, EQ3, 1'b0);
  Priority_Encoder #(.select(2), .disabled(0)) \u_шифратор  (
    .in0(H0), .in1(H1), .in2(H2), .in3(H3), .out(IDX), .gs(HIT));  // open: en_out, en_in
  Multiplexer #(.select(2), .width(8), .enable("false")) multiplexer_1 (
    .in0(8'h19), .in1({8{1'b0}}), .in2({8{1'b0}}), .in3({8{1'b0}}), .out(PA[20:13]), .sel(IDX));
  not not_1 (Page_Fault, HIT);
  LED u_Page_Fault (.in(Page_Fault));
  // Probe on VA[19:13]
  // Probe on PA[20:13]
  // Probe on {PA[20:13], VA[12:0]}

  assign Offset = VA[12:0];
  assign PA[12:0] = VA[12:0];
  assign PFN = PA[20:13];
  assign VPN = VA[19:13];

  // Other names for the same wires on the sheet: PF = Page_Fault

  // Notes on the sheet:
  //   Виртуальный адрес (20 бит)
  //   TLB (V, VPN, PFN)
  //   Трансляция адреса через TLB: VPN = 11 → PFN = 25, страница 8 КБ (вариант 14)
  //   Физический адрес (21 бит)
endmodule
