// Logisim project pr06_fio.circ as structural Verilog: 2 circuits, main circuit metrics
module metrics (
  input  [7:0] QD__iodepth,
  input  [15:0] \latency__мкс ,
  input  [15:0] \BS__байт ,
  output [31:0] IOPS,
  output [31:0] \BW__байт_с ,
  output [31:0] \BW__КиБ_с 
);

  wire [31:0] BS, LAT, QD, QDM;

  // Probe on QD
  // Probe on LAT
  // Probe on BS
  assign QD = {{24{1'b0}}, QD__iodepth};  // Bit_Extender bit_extender_1
  assign LAT = {{16{1'b0}}, \latency__мкс };  // Bit_Extender bit_extender_2
  assign BS = {{16{1'b0}}, \BS__байт };  // Bit_Extender bit_extender_3
  Multiplier #(.width(32)) multiplier_1 (.a(QD), .b(32'hf4240), .out(QDM));  // open: cin, cout
  Divider #(.width(32)) divider_1 (.a(QDM), .b(LAT), .out(IOPS), .upper({32{1'b0}}));  // open: rem
  Multiplier #(.width(32)) multiplier_2 (.a(IOPS), .b(BS), .out(\BW__байт_с ));  // open: cin, cout
  Shifter #(.width(32), .shift("lr")) shifter_1 (.in(\BW__байт_с ), .\dist (5'b01010), .out(\BW__КиБ_с ));
  // Probe on IOPS
  // Probe on \BW__байт_с 
  // Probe on \BW__КиБ_с 

  // Other names for the same wires on the sheet: BS16[15:0] = \BS__байт ; BWB[31:0] = \BW__байт_с ;
  //   BWK[31:0] = \BW__КиБ_с ; LAT16[15:0] = \latency__мкс ; QD8[7:0] = QD__iodepth

  // Notes on the sheet:
  //   Закон Литтла: IOPS = QD / latency, BW = IOPS · BS
endmodule

module randread (
  output [20:0] \LBA__сектор ,
  output [31:0] \смещение__байт ,
  output [15:0] \запросов 
);

  wire CLK;
  wire [31:0] LBA32;

  Clock \u_такт___1_запрос  (.out(CLK));
  Random #(.width(21), .seed(14)) \u_ГПСЧ  (.clk(CLK), .out(\LBA__сектор ));  // open: next, clr
  Counter #(.width(16), .max('hffff)) \u_Запросов_выдано  (
    .Q(\запросов ), .clk(CLK));  // open: load, D, count, carry, clr
  assign LBA32 = {{11{1'b0}}, \LBA__сектор };  // Bit_Extender bit_extender_1
  Shifter #(.width(32), .shift("ll")) shifter_1 (.in(LBA32), .\dist (5'b01001), .out(\смещение__байт ));
  // Probe on \LBA__сектор 
  // Probe on \смещение__байт 
  // Probe on \запросов 

  // Other names for the same wires on the sheet: CNT[15:0] = \запросов ; LBA[20:0] = \LBA__сектор ;
  //   OFS[31:0] = \смещение__байт 

  // Notes on the sheet:
  //   Генератор случайного чтения: --rw=randread --bs=512 --size=1G
endmodule
