// Logisim project pr07_pic.circ as structural Verilog: 1 circuit, main circuit PIC
module PIC (
  input  IRQ0_HDD,
  input  \IRQ1_Тачпад ,
  input  \IRQ2_Клавиатура ,
  input  \IRQ3_Плоттер ,
  input  [15:0] \PC__текущая_команда ,
  input  IRET,
  input  CLK,
  output INT,
  output [15:0] VEC,
  output [15:0] RET,
  output [2:0] LVL,
  output [1:0] SP
);

  wire ALLOW, ANY, HIGHER, IDLE, NINT, POP, STEP;
  wire [1:0] PRI, REQ, SADDR, SPDEC, SPINC, SPN;
  wire [2:0] LVLN, RLVL, RQLV;
  wire [15:0] NEXT;

  LED \INT__запрос_принят  (.in(INT));
  // Probe on REQ
  // Probe on VEC
  // Probe on NEXT
  // Probe on RET
  // Probe on LVL
  Priority_Encoder #(.select(2), .disabled(0)) priority_encoder_1 (
    .in0(\IRQ3_Плоттер ), .in1(\IRQ2_Клавиатура ), .in2(\IRQ1_Тачпад ), .in3(IRQ0_HDD), .out(PRI), .gs(ANY));  // open: en_out, en_in
  Adder #(.width(3)) adder_1 (.a({1'b0, REQ}), .b(3'b001), .out(RQLV));  // open: cin, cout
  Subtractor #(.width(2)) subtractor_1 (.a(2'b11), .b(PRI), .out(REQ));  // open: bin, bout
  Comparator #(.width(3), .mode("unsigned")) comparator_1 (.a(RQLV), .b(LVL), .lt(HIGHER));  // open: gt, eq
  Comparator #(.width(3), .mode("unsigned")) comparator_2 (.a(LVL), .b(3'b000), .eq(IDLE));  // open: gt, lt
  Multiplexer #(.select(2), .width(16), .enable("true"), .disabled(0)) IDT (
    .in0(16'h65), .in1(16'hc9), .in2(16'h12d), .in3(16'h191), .out(VEC), .sel(REQ), .en(ANY));
  or or_1 (ALLOW, HIGHER, IDLE);
  not not_1 (NINT, INT);
  and and_1 (INT, ANY, ALLOW);
  and and_2 (POP, IRET, NINT);
  or or_2 (STEP, INT, POP);
  Adder #(.width(16)) adder_2 (.a(\PC__текущая_команда ), .b(16'h1), .out(NEXT));  // open: cin, cout
  Adder #(.width(2)) adder_3 (.a(SP), .b(2'b01), .out(SPINC));  // open: cin, cout
  Subtractor #(.width(2)) subtractor_2 (.a(SP), .b(2'b01), .out(SPDEC));  // open: bin, bout
  Multiplexer #(.select(1), .width(2), .enable("false")) multiplexer_1 (.in0(SPDEC), .in1(SPINC), .out(SPN), .sel(INT));
  Multiplexer #(.select(1), .width(2), .enable("false")) multiplexer_2 (.in0(SPDEC), .in1(SP), .out(SADDR), .sel(INT));
  Multiplexer #(.select(1), .width(3), .enable("false")) multiplexer_3 (.in0(RLVL), .in1(RQLV), .out(LVLN), .sel(INT));
  Register #(.width(2)) u_SP (.D(SPN), .en(STEP), .Q(SP), .clk(CLK));  // open: clr
  Register #(.width(3)) u_LVL (.D(LVLN), .en(STEP), .Q(LVL), .clk(CLK));  // open: clr
  RAM #(.addrWidth(2), .dataWidth(19), .bus("separate")) \u_Стек  (
    .addr(SADDR), .din({LVL, NEXT}), .data({RLVL, RET}), .str(INT), .clk(CLK), .ld(1'b1));  // open: sel, clr

  // Other names for the same wires on the sheet: IRQ0 = IRQ0_HDD; IRQ1 = \IRQ1_Тачпад ; IRQ2 = \IRQ2_Клавиатура ;
  //   IRQ3 = \IRQ3_Плоттер ; PC[15:0] = \PC__текущая_команда ; REQ3[1:0] = REQ; SDIN[18:0] = {LVL, NEXT};
  //   STOP[18:0] = {RLVL, RET}

  // Notes on the sheet:
  //   IRQ запроса
  //   Вектор (адрес ПОП)
  //   Адрес возврата
  //   Вершина стека
  //   LVL (0 — осн. программа)
  //   Приоритетный контроллер прерываний и стек возвратов (вариант 14)
endmodule
