// Logisim project pr11.circ as structural Verilog: 3 circuits, main circuit main
module main (
  output [15:0] SUM_SEQ,
  output [4:0] T_SEQ,
  output DONE_SEQ,
  output [15:0] SUM_PAR,
  output [2:0] T_PAR,
  output DONE_PAR,
  output halt
);

  seq seq_1 (.SUM(SUM_SEQ), .T(T_SEQ), .DONE(DONE_SEQ));
  par par_1 (.SUM(SUM_PAR), .T(T_PAR), .DONE(DONE_PAR));
  // Probe on SUM_SEQ
  // Probe on T_SEQ
  // Probe on SUM_PAR
  // Probe on T_PAR
  and and_1 (halt, DONE_SEQ, DONE_PAR);

  // Other names for the same wires on the sheet: D_PAR = DONE_PAR; D_SEQ = DONE_SEQ

  // Notes on the sheet:
  //   seq
  //   par
  //   Сравнение: последовательное (seq) и параллельное (par) суммирование
  //   Σ yᵢ = 4488;  seq: 16 тактов,  par: 16/4 + 1 = 5 тактов
  //   halt = DONE_SEQ ∧ DONE_PAR
endmodule

module seq (
  output [15:0] SUM,
  output [4:0] T,
  output DONE
);

  wire CLK;
  wire [15:0] adder_1_out, rom_1_data;

  Clock u_CLK (.out(CLK));
  Counter #(.width(5), .max('h10), .ongoal("stay")) u_t (.Q(T), .carry(DONE), .clk(CLK));  // open: load, D, count, clr
  ROM #(.addrWidth(5), .dataWidth(16)) rom_1 (.addr(T), .data(rom_1_data));  // open: sel
  Adder #(.width(16)) adder_1 (.a(SUM), .b(rom_1_data), .out(adder_1_out));  // open: cin, cout
  Register #(.width(16)) ACC (.D(adder_1_out), .Q(SUM), .clk(CLK));  // open: en, clr
  // Probe on SUM
  // Probe on T

  // Notes on the sheet:
  //   счётчик тактов t (стоп при t = 16)
  //   Последовательное суммирование: N = 16 элементов, 1 элемент за такт
  //   ACC ← ACC + ROM[t];  yᵢ = 3·xᵢ², xᵢ = 1…16;  результат через 16 тактов
  //   ROM: y₀ … y₁₅
  //   contents of rom_1 (hex, n*v repeats v):
  //   3 c 1b 30 4b 6c 93 c0 f3 12c 16b 1b0 1fb 24c 2a3 300
  //   сумматор + регистр ACC (накопитель)
endmodule

module par (
  output [15:0] SUM,
  output [2:0] T,
  output DONE
);

  wire CLK, RED;
  wire [15:0] adder_1_out, adder_2_out, adder_3_out, adder_4_out, adder_5_out, adder_6_out, adder_7_out,
       rom_1_data, rom_2_data, rom_3_data, rom_4_data, S0_q, S1_q, S2_q, S3_q;

  Clock u_CLK (.out(CLK));
  Counter #(.width(3), .max('h5), .ongoal("stay")) u_t (.Q(T), .carry(DONE), .clk(CLK));  // open: load, D, count, clr
  ROM #(.addrWidth(3), .dataWidth(16)) rom_1 (.addr(T), .data(rom_1_data));  // open: sel
  ROM #(.addrWidth(3), .dataWidth(16)) rom_2 (.addr(T), .data(rom_2_data));  // open: sel
  ROM #(.addrWidth(3), .dataWidth(16)) rom_3 (.addr(T), .data(rom_3_data));  // open: sel
  ROM #(.addrWidth(3), .dataWidth(16)) rom_4 (.addr(T), .data(rom_4_data));  // open: sel
  Comparator #(.width(3), .mode("unsigned")) comparator_1 (.a(T), .b(3'b100), .eq(RED));  // open: gt, lt
  Adder #(.width(16)) adder_1 (.a(S0_q), .b(rom_1_data), .out(adder_1_out));  // open: cin, cout
  Adder #(.width(16)) adder_2 (.a(S1_q), .b(rom_2_data), .out(adder_2_out));  // open: cin, cout
  Adder #(.width(16)) adder_3 (.a(S2_q), .b(rom_3_data), .out(adder_3_out));  // open: cin, cout
  Adder #(.width(16)) adder_4 (.a(S3_q), .b(rom_4_data), .out(adder_4_out));  // open: cin, cout
  Register #(.width(16)) S0 (.D(adder_1_out), .Q(S0_q), .clk(CLK));  // open: en, clr
  Register #(.width(16)) S1 (.D(adder_2_out), .Q(S1_q), .clk(CLK));  // open: en, clr
  Register #(.width(16)) S2 (.D(adder_3_out), .Q(S2_q), .clk(CLK));  // open: en, clr
  Register #(.width(16)) S3 (.D(adder_4_out), .Q(S3_q), .clk(CLK));  // open: en, clr
  // Probe on S0_q
  // Probe on S1_q
  // Probe on S2_q
  // Probe on S3_q
  Adder #(.width(16)) adder_5 (.a(S0_q), .b(S1_q), .out(adder_5_out));  // open: cin, cout
  Adder #(.width(16)) adder_6 (.a(S2_q), .b(S3_q), .out(adder_6_out));  // open: cin, cout
  Adder #(.width(16)) adder_7 (.a(adder_5_out), .b(adder_6_out), .out(adder_7_out));  // open: cin, cout
  Register #(.width(16)) RES (.D(adder_7_out), .en(RED), .Q(SUM), .clk(CLK));  // open: clr
  // Probe on SUM
  // Probe on T

  // Notes on the sheet:
  //   счётчик тактов t (стоп при t = 5)
  //   t = 4 → такт редукции
  //   ПЭ0: x = 1…4
  //   contents of rom_1 (hex, n*v repeats v):
  //   3 c 1b 30
  //   ПЭ1: x = 5…8
  //   contents of rom_2 (hex, n*v repeats v):
  //   4b 6c 93 c0
  //   ПЭ2: x = 9…12
  //   contents of rom_3 (hex, n*v repeats v):
  //   f3 12c 16b 1b0
  //   ПЭ3: x = 13…16
  //   contents of rom_4 (hex, n*v repeats v):
  //   1fb 24c 2a3 300
  //   Параллельное суммирование: P = 4 накопителя по N/P = 4 элемента + дерево редукции
  //   ПЭj: Sj ← Sj + ROMj[t] (такты 1–4);  такт 5: RES ← (S0 + S1) + (S2 + S3)
  //   S0 + S1
  //   S2 + S3
  //   дерево редукции (reduce)
endmodule
