// Logisim project pr12.circ as structural Verilog: 2 circuits, main circuit simt4
module simt4 (
  input  RESTART,
  output [15:0] ZX0,
  output [15:0] ZY0,
  output [7:0] N0,
  output ESC0,
  output [15:0] ZX1,
  output [15:0] ZY1,
  output [7:0] N1,
  output ESC1,
  output [15:0] ZX2,
  output [15:0] ZY2,
  output halt,
  output [7:0] N2,
  output ESC2,
  output [7:0] STEP,
  output [15:0] ZX3,
  output [15:0] ZY3,
  output [3:0] ESCMASK,
  output [7:0] N3,
  output ESC3
);

  wire ALLESC, CLK, comparator_1_eq, LOAD, START_qn;
  wire [7:0] multiplexer_1_out, STEP1;

  Clock u_CLK (.out(CLK));
  Multiplexer #(.width(8), .enable("false")) multiplexer_1 (
    .in0(STEP1), .in1({8{1'b0}}), .out(multiplexer_1_out), .sel(LOAD));
  D_Flip_Flop START (.clk(CLK), .D(1'b1), .Qn(START_qn));  // open: Q, preset, en, reset
  Register #(.width(8)) u_STEP (.D(multiplexer_1_out), .Q(STEP), .clk(CLK));  // open: en, clr
  or or_1 (LOAD, START_qn, RESTART);
  Adder #(.width(8)) adder_1 (.a(STEP), .b(8'h1), .out(STEP1));  // open: cin, cout
  Comparator #(.width(8), .mode("unsigned")) comparator_1 (.a(STEP), .b(8'h20), .eq(comparator_1_eq));  // open: gt, lt
  or or_2 (halt, comparator_1_eq, ALLESC);
  // Probe on STEP
  Comparator #(.width(4), .mode("unsigned")) comparator_2 (
    .a({ESC3, ESC2, ESC1, ESC0}), .b(4'b1111), .eq(ALLESC));  // open: gt, lt
  julia_lane lane0 (
    .Z0X(16'hf97e), .Z0Y(16'hfe35), .KX(16'hf333), .KY(16'h27f), .LOAD(LOAD), .CLK(CLK), .ZX(ZX0), .ZY(ZY0),
    .N(N0), .ESC(ESC0));
  julia_lane lane1 (
    .Z0X(16'h42a), .Z0Y(16'hfe35), .KX(16'hf333), .KY(16'h27f), .LOAD(LOAD), .CLK(CLK), .ZX(ZX1), .ZY(ZY1),
    .N(N1), .ESC(ESC1));
  julia_lane lane2 (
    .Z0X(16'h689), .Z0Y(16'hfe35), .KX(16'hf333), .KY(16'h27f), .LOAD(LOAD), .CLK(CLK), .ZX(ZX2), .ZY(ZY2),
    .N(N2), .ESC(ESC2));
  julia_lane lane3 (
    .Z0X(16'hfed4), .Z0Y(16'hfe35), .KX(16'hf333), .KY(16'h27f), .LOAD(LOAD), .CLK(CLK), .ZX(ZX3), .ZY(ZY3),
    .N(N3), .ESC(ESC3));
  // Probe on ZX0
  // Probe on ZY0
  // Probe on N0
  // Probe on ZX1
  // Probe on ZY1
  // Probe on N1
  // Probe on ZX2
  // Probe on ZY2
  // Probe on N2
  // Probe on ZX3
  // Probe on ZY3
  // Probe on N3

  assign ESCMASK = {ESC3, ESC2, ESC1, ESC0};

  // Notes on the sheet:
  //   kx, ky (Q4.12), общие для всех линий
  //   Устройство управления
  //   LOAD = 1 на первом такте (загрузка z0), далее ITER
  //   маска ушедших линий
  //   halt: STEP = 32 или все линии ушли
  //   все линии ушли?
  //   SIMT: 4 линии выполняют одну общую команду над 4 пикселями (вариант 14, k = -0.8 + 0.156i)
  //   пиксель 0
  //   (740, 600)
  //   пиксель 1
  //   (1100, 600)
  //   пиксель 2
  //   (1180, 600)
  //   пиксель 3
  //   (920, 600)
endmodule

module julia_lane (
  input  [15:0] Z0X,
  input  [15:0] Z0Y,
  input  [15:0] KX,
  input  [15:0] KY,
  input  LOAD,
  input  CLK,
  output [15:0] ZX,
  output [15:0] ZY,
  output [7:0] N,
  output ESC
);

  wire not_1_out, WE;
  wire [7:0] multiplexer_3_out, N1;
  wire [15:0] multiplexer_1_out, multiplexer_2_out, ZXN, ZYN;
  wire [31:0] adder_1_out, multiplier_1_out, multiplier_2_out, multiplier_3_out, subtractor_1_out, SX, SY;

  Multiplexer #(.width(16), .enable("false")) multiplexer_1 (.in0(ZXN), .in1(Z0X), .out(multiplexer_1_out), .sel(LOAD));
  Multiplexer #(.width(16), .enable("false")) multiplexer_2 (.in0(ZYN), .in1(Z0Y), .out(multiplexer_2_out), .sel(LOAD));
  Register #(.width(16)) RZX (.D(multiplexer_1_out), .en(WE), .Q(ZX), .clk(CLK));  // open: clr
  Register #(.width(16)) RZY (.D(multiplexer_2_out), .en(WE), .Q(ZY), .clk(CLK));  // open: clr
  not not_1 (not_1_out, ESC);
  or or_1 (WE, not_1_out, LOAD);
  assign SX = {{16{ZX[15]}}, ZX};  // Bit_Extender bit_extender_1
  assign SY = {{16{ZY[15]}}, ZY};  // Bit_Extender bit_extender_2
  Multiplexer #(.width(8), .enable("false")) multiplexer_3 (
    .in0(N1), .in1({8{1'b0}}), .out(multiplexer_3_out), .sel(LOAD));
  Multiplier #(.width(32)) multiplier_1 (.a(SX), .b(SX), .out(multiplier_1_out));  // open: cin, cout
  Multiplier #(.width(32)) multiplier_2 (.a(SY), .b(SY), .out(multiplier_2_out));  // open: cin, cout
  Multiplier #(.width(32)) multiplier_3 (.a(SX), .b(SY), .out(multiplier_3_out));  // open: cin, cout
  Register #(.width(8)) RN (.D(multiplexer_3_out), .en(WE), .Q(N), .clk(CLK));  // open: clr
  Adder #(.width(32)) adder_1 (.a(multiplier_1_out), .b(multiplier_2_out), .out(adder_1_out));  // open: cin, cout
  Subtractor #(.width(32)) subtractor_1 (
    .a(multiplier_1_out), .b(multiplier_2_out), .out(subtractor_1_out));  // open: bin, bout
  Adder #(.width(8)) adder_2 (.a(N), .b(8'h1), .out(N1));  // open: cin, cout
  Comparator #(.width(32)) comparator_1 (.a(adder_1_out), .b(32'h4000000), .gt(ESC));  // open: eq, lt
  Adder #(.width(16)) adder_3 (.a(subtractor_1_out[27:12]), .b(KX), .out(ZXN));  // open: cin, cout
  Adder #(.width(16)) adder_4 (.a(multiplier_3_out[26:11]), .b(KY), .out(ZYN));  // open: cin, cout

  // Notes on the sheet:
  //   регистр zx
  //   регистр zy
  //   маска: линия активна, пока |z|^2 <= 4
  //   знаковое расширение 16->32
  //   Ядро-линия SIMT: одна итерация z <- z^2 + k за такт (Q4.12)
  //   zx*zx
  //   zy*zy
  //   zx*zy
  //   |z|^2
  //   4.0 (Q8.24)
  //   счётчик итераций N (8 бит)
  //   биты 27..12
  //   биты 26..11 (x2)
  //   |z|^2 > 4.0 ?
  //   zx' = zx^2 - zy^2 + kx
  //   zy' = 2*zx*zy + ky
endmodule
