// Logisim project pr01.circ as structural Verilog: 3 circuits, main circuit xor_cmos
module xor_cmos (
  input  A,
  input  B,
  output Y
);

  wire G1, G2, G3, transistor_3_out, transistor_6_out, transistor_11_out, transistor_14_out;

  Transistor #(.\type ("p")) transistor_1 (.in(1'b1), .out(G1), .gate(A));
  Transistor #(.\type ("n")) transistor_2 (.in(transistor_3_out), .out(G1), .gate(A));
  Transistor #(.\type ("n")) transistor_3 (.in(1'b0), .out(transistor_3_out), .gate(B));
  Transistor #(.\type ("p")) transistor_4 (.in(1'b1), .out(G3), .gate(B));
  Transistor #(.\type ("n")) transistor_5 (.in(transistor_6_out), .out(G3), .gate(B));
  Transistor #(.\type ("n")) transistor_6 (.in(1'b0), .out(transistor_6_out), .gate(G1));
  Transistor #(.\type ("p")) transistor_7 (.in(1'b1), .out(G1), .gate(B));
  Transistor #(.\type ("p")) transistor_8 (.in(1'b1), .out(G3), .gate(G1));
  Transistor #(.\type ("p")) transistor_9 (.in(1'b1), .out(G2), .gate(A));
  Transistor #(.\type ("n")) transistor_10 (.in(transistor_11_out), .out(G2), .gate(A));
  Transistor #(.\type ("n")) transistor_11 (.in(1'b0), .out(transistor_11_out), .gate(G1));
  Transistor #(.\type ("p")) transistor_12 (.in(1'b1), .out(Y), .gate(G2));
  Transistor #(.\type ("n")) transistor_13 (.in(transistor_14_out), .out(Y), .gate(G2));
  Transistor #(.\type ("n")) transistor_14 (.in(1'b0), .out(transistor_14_out), .gate(G3));
  Transistor #(.\type ("p")) transistor_15 (.in(1'b1), .out(G2), .gate(G1));
  Transistor #(.\type ("p")) transistor_16 (.in(1'b1), .out(Y), .gate(G3));

  // Other names for the same wires on the sheet: XOR = Y

  // Notes on the sheet:
  //   И-НЕ 1: G1 = A·B
  //   И-НЕ 3: G3 = B·G1
  //   Элемент «Исключающее ИЛИ» на транзисторах (базис И-НЕ, 4 ячейки КМОП И-НЕ)
  //   И-НЕ 2: G2 = A·G1
  //   И-НЕ 4: XOR = G2·G3
endmodule

module F_sknf (
  input  a,
  input  b,
  input  c,
  input  d,
  output F
);

  wire na, nb, nc, nd, or_1_out, or_2_out, or_3_out, or_4_out, or_5_out, or_6_out, or_7_out, or_8_out,
       or_9_out;

  not not_1 (na, a);
  not not_2 (nb, b);
  not not_3 (nc, c);
  not not_4 (nd, d);
  or or_1 (or_1_out, a, b, nc, nd);
  or or_2 (or_2_out, a, nb, c, d);
  or or_3 (or_3_out, a, nb, c, nd);
  or or_4 (or_4_out, a, nb, nc, d);
  or or_5 (or_5_out, a, nb, nc, nd);
  or or_6 (or_6_out, na, b, nc, nd);
  or or_7 (or_7_out, na, nb, c, d);
  or or_8 (or_8_out, na, nb, c, nd);
  or or_9 (or_9_out, na, nb, nc, d);
  and and_1 (F, or_1_out, or_2_out, or_3_out, or_4_out, or_5_out, or_6_out, or_7_out, or_8_out, or_9_out);

  // Notes on the sheet:
  //   F = E0E1: схема по СКНФ (9 конституент нуля)
  //   M3
  //   M4
  //   M5
  //   M6
  //   M7
  //   M11
  //   M12
  //   M13
  //   M14
endmodule

module F_mdnf (
  input  a,
  input  b,
  input  c,
  input  d,
  output F
);

  wire and_1_out, and_2_out, and_3_out, na, nb, nc, nd;

  not not_1 (na, a);
  not not_2 (nb, b);
  not not_3 (nc, c);
  not not_4 (nd, d);
  and and_1 (and_1_out, nb, nd);
  and and_2 (and_2_out, nb, nc);
  and and_3 (and_3_out, a, b, c, d);
  or or_1 (F, and_1_out, and_2_out, and_3_out);

  // Notes on the sheet:
  //   F = E0E1: схема по МДНФ  F = ¬b·¬d ∨ ¬b·¬c ∨ a·b·c·d
endmodule
