// Logisim project decoder.circ as structural Verilog: 1 circuit, main circuit decoder_4_16
module decoder_4_16 (
  input  A0,
  input  A1,
  input  A2,
  input  A3,
  output Y0,
  output Y1,
  output Y2,
  output Y3,
  output Y4,
  output Y5,
  output Y6,
  output Y7,
  output Y8,
  output Y9,
  output Y10,
  output Y11,
  output Y12,
  output Y13,
  output Y14,
  output Y15
);

  Decoder #(.select(4)) decoder_1 (
    .out0(Y0), .out1(Y1), .out2(Y2), .out3(Y3), .out4(Y4), .out5(Y5), .out6(Y6), .out7(Y7), .out8(Y8),
    .out9(Y9), .out10(Y10), .out11(Y11), .out12(Y12), .out13(Y13), .out14(Y14), .out15(Y15),
    .sel({A3, A2, A1, A0}), .en(1'b1));

  // Other names for the same wires on the sheet: ADDR[3:0] = {A3, A2, A1, A0}

  // Notes on the sheet:
  //   Дешифратор 4→16: адрес A3A2A1A0 активирует выход Y<номер> (EN=1)
endmodule
