// Logisim project jk.circ as structural Verilog: 1 circuit, main circuit jk_trigger
module jk_trigger (
  input  J,
  input  K,
  output Q,
  output nQ
);

  wire CLK;

  Clock u_CLK (.out(CLK));
  J_K_Flip_Flop j_k_ff_1 (.J(J), .clk(CLK), .K(K), .Q(Q), .Qn(nQ));  // open: preset, en, reset
  LED u_Q (.in(Q));

  // Notes on the sheet:
  //   JK-триггер: J,K — входы, CLK — синхросигнал, Q/¬Q — выходы
endmodule
