// Logisim project mux.circ as structural Verilog: 1 circuit, main circuit mux_16_1
module mux_16_1 (
  input  D0,
  input  D1,
  input  D2,
  input  D3,
  input  D4,
  input  D5,
  input  D6,
  input  D7,
  input  D8,
  input  D9,
  input  D10,
  input  D11,
  input  D12,
  input  D13,
  input  D14,
  input  D15,
  input  A0,
  input  A1,
  input  A2,
  input  A3,
  output Y
);

  Multiplexer #(.select(4), .enable("false")) multiplexer_1 (
    .in0(D0), .in1(D1), .in2(D2), .in3(D3), .in4(D4), .in5(D5), .in6(D6), .in7(D7), .in8(D8), .in9(D9),
    .in10(D10), .in11(D11), .in12(D12), .in13(D13), .in14(D14), .in15(D15), .out(Y), .sel({A3, A2, A1, A0}));
  LED u_Y (.in(Y));

  // Other names for the same wires on the sheet: ADDR[3:0] = {A3, A2, A1, A0}

  // Notes on the sheet:
  //   Мультиплексор 16→1: адрес A3A2A1A0 выбирает вход D<номер> на выход Y
endmodule
