// Logisim project pr03_ou.circ as structural Verilog: 2 circuits, main circuit OU
module OU (
  input  [2:0] MSA,
  input  [2:0] MSB,
  input  F,
  input  M,
  input  S2,
  input  S1,
  input  S0,
  input  C0,
  input  E,
  input  [2:0] DC,
  input  MSM,
  input  WR,
  input  CLK,
  input  [15:0] \Ввод ,
  output [15:0] \S_шина 
);

  wire CF, en1, en2, en3, en4, en5, en6, en7;
  wire [3:0] FL, FLAGS;
  wire [11:0] A12;
  wire [15:0] AC, InpR, IR, MDR, MDRIN, OPA, OPB, OutR, PC, RAMOUT;
  wire [15:12] MAR;

  Multiplexer #(.select(1), .width(16), .enable("false")) MS_M (.in0(\S_шина ), .in1(RAMOUT), .out(MDRIN), .sel(MSM));
  Decoder #(.select(3), .enable("true"), .disabled(0)) u_DC (
    .out1(en1), .out2(en2), .out3(en3), .out4(en4), .out5(en5), .out6(en6), .out7(en7), .sel(DC), .en(E));  // open: out0
  Register #(.width(16)) u_OutR (.D(\S_шина ), .en(en1), .Q(OutR), .clk(CLK));  // open: clr
  Register #(.width(16)) u_InpR (.D(\S_шина ), .en(en2), .Q(InpR), .clk(CLK));  // open: clr
  Register #(.width(16)) u_MDR (.D(MDRIN), .en(en3), .Q(MDR), .clk(CLK));  // open: clr
  Register #(.width(16)) u_MAR (.D(\S_шина ), .en(en4), .Q({MAR, A12}), .clk(CLK));  // open: clr
  Register #(.width(16)) u_IR (.D(\S_шина ), .en(en5), .Q(IR), .clk(CLK));  // open: clr
  Register #(.width(16)) u_AC (.D(\S_шина ), .en(en6), .Q(AC), .clk(CLK));  // open: clr
  Register #(.width(16)) u_PC (.D(\S_шина ), .en(en7), .Q(PC), .clk(CLK));  // open: clr
  Multiplexer #(.select(3), .width(16), .enable("false")) MS_A (
    .in0(PC), .in1(AC), .in2(IR), .in3({MAR, A12}), .in4(MDR), .in5(InpR), .in6(OutR), .in7(\Ввод ),
    .out(OPA), .sel(MSA));
  Multiplexer #(.select(3), .width(16), .enable("false")) MS_B (
    .in0(PC), .in1(AC), .in2(IR), .in3({MAR, A12}), .in4(MDR), .in5(InpR), .in6(OutR), .in7(\Ввод ),
    .out(OPB), .sel(MSB));
  ALU ALU (
    .A(OPA), .B(OPB), .F(F), .M(M), .S2(S2), .S1(S1), .S0(S0), .C0(C0), .R(\S_шина ), .Z(FLAGS[0]),
    .S(FLAGS[1]), .C(CF), .V(FLAGS[3]));
  RAM #(.addrWidth(12), .dataWidth(16), .bus("separate")) RAM (
    .addr(A12), .din(MDR), .data(RAMOUT), .str(WR), .clk(CLK), .ld(1'b1));  // open: sel, clr
  Register #(.width(4)) u_Flags (.D({FLAGS[3], CF, FLAGS[1:0]}), .en(E), .Q(FL), .clk(CLK));  // open: clr

  // Other names for the same wires on the sheet: Z = FLAGS[0]; SF = FLAGS[1]; FLAGS[2] = CF; VF = FLAGS[3];
  //   IN[15:0] = \Ввод ; MAR[11:0] = A12; S[15:0] = \S_шина 

  // Notes on the sheet:
  //   Управляющее слово
  //   Учебное операционное устройство (рис. 3.4). Вариант 23: OUTR ← AC NOR OUTR
endmodule

module ALU (
  input  [15:0] A,
  input  [15:0] B,
  input  F,
  input  M,
  input  S2,
  input  S1,
  input  S0,
  input  C0,
  output [15:0] R,
  output Z,
  output S,
  output C,
  output V
);

  wire ARS, CO, SGN_CH, SGN_EQ;
  wire [15:0] AND, ARITH, ASR, BMA, LOG, nA, NAND, nB, NOR, OR, R0, R1, ROL, ROL2, ROR, ROR2, SHL, SHR, XNOR,
       XOR, Y;

  assign nB = ~B;  // NOT_Gate not_1, 16 bits wide
  assign nA = ~A;  // NOT_Gate not_2, 16 bits wide
  Multiplexer #(.select(2), .width(16), .enable("false")) multiplexer_1 (
    .in0({16{1'b0}}), .in1(B), .in2(nB), .in3({16{1'b1}}), .out(Y), .sel({S1, S0}));
  Adder #(.width(16)) adder_1 (.a(A), .b(Y), .out(ARITH), .cin(C0), .cout(CO));
  Adder #(.width(16)) adder_2 (.a(B), .b(nA), .out(BMA), .cin(C0));  // open: cout
  assign OR = A | B;  // OR_Gate or_1, 16 bits wide
  assign XOR = A ^ B;  // XOR_Gate xor_1, 16 bits wide
  assign AND = A & B;  // AND_Gate and_1, 16 bits wide
  assign NAND = ~(A & B);  // NAND_Gate nand_1, 16 bits wide
  assign NOR = ~(A | B);  // NOR_Gate nor_1, 16 bits wide
  assign XNOR = ~(A ^ B);  // XNOR_Gate xnor_1, 16 bits wide
  Multiplexer #(.select(2), .width(16), .enable("false")) multiplexer_2 (
    .in0(OR), .in1(XOR), .in2(AND), .in3(nA), .out(LOG), .sel({S1, S0}));
  Shifter #(.width(16), .shift("ll")) shifter_1 (.in(A), .\dist (4'b0001), .out(SHL));
  Shifter #(.width(16), .shift("lr")) shifter_2 (.in(A), .\dist (4'b0001), .out(SHR));
  Shifter #(.width(16), .shift("rl")) shifter_3 (.in(A), .\dist (4'b0001), .out(ROL));
  Shifter #(.width(16), .shift("rr")) shifter_4 (.in(A), .\dist (4'b0001), .out(ROR));
  Shifter #(.width(16), .shift("ar")) shifter_5 (.in(A), .\dist (4'b0001), .out(ASR));
  Shifter #(.width(16), .shift("rl")) shifter_6 (.in(A), .\dist (4'b0010), .out(ROL2));
  Shifter #(.width(16), .shift("rr")) shifter_7 (.in(A), .\dist (4'b0010), .out(ROR2));
  xnor xnor_2 (SGN_EQ, A[15], Y[15]);
  xor xor_2 (SGN_CH, A[15], R[15]);
  Comparator #(.width(16)) comparator_1 (.a(R), .b({16{1'b0}}), .eq(Z));  // open: gt, lt
  Multiplexer #(.select(2), .width(16), .enable("false")) multiplexer_3 (
    .in0(ARITH), .in1(LOG), .in2({16{1'b0}}), .in3({16{1'b0}}), .out(R0), .sel({M, S2}));
  nor nor_2 (ARS, F, M, S2);
  and and_2 (C, CO, ARS);
  and and_3 (V, SGN_EQ, SGN_CH, ARS);
  Multiplexer #(.select(4), .width(16), .enable("false")) multiplexer_4 (
    .in0(BMA), .in1(NAND), .in2(NOR), .in3(XNOR), .in4({16{1'b0}}), .in5({16{1'b0}}), .in6({16{1'b0}}),
    .in7({16{1'b0}}), .in8(SHL), .in9(SHR), .in10(ROL), .in11(ROR), .in12(SHL), .in13(ASR), .in14(ROL2),
    .in15(ROR2), .out(R1), .sel({M, S2, S1, S0}));
  Multiplexer #(.select(1), .width(16), .enable("false")) multiplexer_5 (.in0(R0), .in1(R1), .out(R), .sel(F));

  assign S = R[15];

  // Other names for the same wires on the sheet: MS210[3:0] = {M, S2, S1, S0}; S10[1:0] = {S1, S0};
  //   MS2[1:0] = {M, S2}; SF = R[15]

  // Notes on the sheet:
  //   АЛУ 16 разрядов (табл. 3.1): код F M S2 S1 S0 C0
endmodule
