// Logisim project pr05_tlb.circ as structural Verilog: 1 circuit, main circuit TLB
module TLB (
  input  [19:0] VA,
  output HIT,
  output Page_Fault,
  output [8:0] VPN,
  output [10:0] Offset,
  output [7:0] PFN,
  output [18:0] PA
);

  wire EQ0, EQ1, EQ2, EQ3, H0, H1, H2, H3;
  wire [1:0] IDX;

  // Probe on VA
  Comparator #(.width(9), .mode("unsigned")) comparator_1 (.a(VA[19:11]), .b(9'h4), .eq(EQ0));  // open: gt, lt
  Comparator #(.width(9), .mode("unsigned")) comparator_2 (.a(VA[19:11]), .b({9{1'b0}}), .eq(EQ1));  // open: gt, lt
  Comparator #(.width(9), .mode("unsigned")) comparator_3 (.a(VA[19:11]), .b({9{1'b0}}), .eq(EQ2));  // open: gt, lt
  Comparator #(.width(9), .mode("unsigned")) comparator_4 (.a(VA[19:11]), .b({9{1'b0}}), .eq(EQ3));  // open: gt, lt
  and and_1 (H0, EQ0, 1'b1);
  and and_2 (H1, EQ1, 1'b0);
  and and_3 (H2, EQ2, 1'b0);
  and and_4 (H3, EQ3, 1'b0);
  Priority_Encoder #(.select(2), .disabled(0)) \u_шифратор  (
    .in0(H0), .in1(H1), .in2(H2), .in3(H3), .out(IDX), .gs(HIT));  // open: en_out, en_in
  Multiplexer #(.select(2), .width(8), .enable("false")) multiplexer_1 (
    .in0(8'ha), .in1({8{1'b0}}), .in2({8{1'b0}}), .in3({8{1'b0}}), .out(PA[18:11]), .sel(IDX));
  not not_1 (Page_Fault, HIT);
  LED u_Page_Fault (.in(Page_Fault));
  // Probe on VA[19:11]
  // Probe on PA[18:11]
  // Probe on {PA[18:11], VA[10:0]}

  assign Offset = VA[10:0];
  assign PA[10:0] = VA[10:0];
  assign PFN = PA[18:11];
  assign VPN = VA[19:11];

  // Other names for the same wires on the sheet: PF = Page_Fault

  // Notes on the sheet:
  //   Виртуальный адрес (20 бит)
  //   TLB (V, VPN, PFN)
  //   Трансляция адреса через TLB: VPN = 4 → PFN = 10, страница 2 КБ (вариант 23)
  //   Физический адрес (21 бит)
endmodule
