// Logisim project counter.circ as structural Verilog: 2 circuits, main circuit counter
module counter (
  input  A,
  input  B,
  output [3:0] Q
);

  wire clk, nA, nB, newQ0, newQ1, newQ2, newQ3, nQ0, nQ1, nQ2, nQ3, R1, R2, R3, R4, R5, R6, st0, st1, st2,
       st3, st4, st5, st6, st7, st8, st9, st10, st11, st12, st13, st14, st15;

  Clock u_clk (.out(clk));
  D_Flip_Flop d_ff_1 (.clk(clk), .D(newQ0), .Q(Q[0]), .Qn(nQ0));  // open: preset, en, reset
  D_Flip_Flop d_ff_2 (.clk(clk), .D(newQ1), .Q(Q[1]), .Qn(nQ1));  // open: preset, en, reset
  and and_1 (st0, nQ3, nQ2, nQ1, nQ0);
  and and_2 (st1, nQ3, nQ2, nQ1, Q[0]);
  and and_3 (st2, nQ3, nQ2, Q[1], nQ0);
  and and_4 (st3, nQ3, nQ2, Q[1], Q[0]);
  and and_5 (st4, nQ3, Q[2], nQ1, nQ0);
  and and_6 (st5, nQ3, Q[2], nQ1, Q[0]);
  and and_7 (st6, nQ3, Q[2], Q[1], nQ0);
  and and_8 (st7, nQ3, Q[2], Q[1], Q[0]);
  D_Flip_Flop d_ff_3 (.clk(clk), .D(newQ2), .Q(Q[2]), .Qn(nQ2));  // open: preset, en, reset
  D_Flip_Flop d_ff_4 (.clk(clk), .D(newQ3), .Q(Q[3]), .Qn(nQ3));  // open: preset, en, reset
  and and_9 (st8, Q[3], nQ2, nQ1, nQ0);
  and and_10 (st9, Q[3], nQ2, nQ1, Q[0]);
  and and_11 (st10, Q[3], nQ2, Q[1], nQ0);
  and and_12 (st11, Q[3], nQ2, Q[1], Q[0]);
  and and_13 (st12, Q[3], Q[2], nQ1, nQ0);
  and and_14 (st13, Q[3], Q[2], nQ1, Q[0]);
  and and_15 (st14, Q[3], Q[2], Q[1], nQ0);
  and and_16 (st15, Q[3], Q[2], Q[1], Q[0]);
  not not_1 (nA, A);
  not not_2 (nB, B);
  and and_17 (R1, A, st4);
  and and_18 (R2, nA, st4);
  and and_19 (R3, B, st11);
  and and_20 (R4, nB, st11);
  and and_21 (R5, B, st7);
  and and_22 (R6, nB, st7);
  Hex_Digit_Display hex_digit_display_1 (.value(Q));  // open: dp
  or or_1 (newQ0, st0, st2, st3, st5, st6, st9, st10, st12, R1, R4);
  or or_2 (newQ1, st5, st6, st8, st12, st14, st15, R2, R4, R6);
  or or_3 (newQ2, st1, st5, st6, st9, st10, st13, R2, R6);
  or or_4 (newQ3, st0, st1, st2, st3, st5, st10, st12, st15, R5, R6);

  // Notes on the sheet:
  //   разряд 0
  //   разряд 1
  //   Счётчик по модулю 16 с произвольным порядком счёта (вариант 29 табл. 2.11), D-триггеры
  //   разряд 2
  //   разряд 3
endmodule

module newQ_min (
  input  Q3,
  input  Q2,
  input  Q1,
  input  Q0,
  input  a,
  input  b,
  output newQ3,
  output newQ2,
  output newQ1,
  output newQ0
);

  wire and_1_out, and_2_out, and_3_out, and_4_out, and_5_out, and_6_out, and_7_out, and_8_out, and_9_out,
       and_10_out, and_11_out, and_12_out, and_13_out, and_14_out, and_15_out, and_16_out, and_17_out,
       and_18_out, and_19_out, and_20_out, and_21_out, and_22_out, and_23_out, and_24_out, and_25_out,
       and_26_out, not_1_out, not_2_out, not_3_out, not_4_out, not_5_out, not_6_out;

  not not_1 (not_1_out, Q3);
  not not_2 (not_2_out, Q2);
  not not_3 (not_3_out, Q1);
  not not_4 (not_4_out, Q0);
  not not_5 (not_5_out, a);
  not not_6 (not_6_out, b);
  and and_1 (and_1_out, not_2_out, Q1, not_4_out);
  and and_2 (and_2_out, Q2, Q1, Q0);
  and and_3 (and_3_out, not_1_out, Q0);
  and and_4 (and_4_out, not_1_out, not_2_out);
  and and_5 (and_5_out, Q3, Q2, not_3_out, not_4_out);
  and and_6 (and_6_out, not_3_out, Q0);
  and and_7 (and_7_out, not_1_out, Q2, Q1, not_4_out);
  and and_8 (and_8_out, Q3, not_2_out, Q1, not_4_out);
  and and_9 (and_9_out, not_1_out, Q2, not_4_out, not_5_out);
  and and_10 (and_10_out, not_1_out, Q2, Q0, not_6_out);
  and and_11 (and_11_out, Q2, Q1, not_4_out);
  and and_12 (and_12_out, not_1_out, Q2, not_3_out, Q0);
  and and_13 (and_13_out, Q3, not_3_out, not_4_out);
  and and_14 (and_14_out, Q3, Q1, Q0, not_6_out);
  and and_15 (and_15_out, Q3, Q2, Q1);
  and and_16 (and_16_out, Q2, not_4_out, not_5_out);
  and and_17 (and_17_out, Q2, Q1, not_6_out);
  and and_18 (and_18_out, not_2_out, Q1, not_4_out);
  and and_19 (and_19_out, not_1_out, Q1, not_4_out);
  and and_20 (and_20_out, not_1_out, not_2_out, not_4_out);
  and and_21 (and_21_out, not_1_out, not_2_out, Q1);
  and and_22 (and_22_out, not_1_out, Q2, not_3_out, Q0);
  and and_23 (and_23_out, Q3, not_2_out, not_3_out, Q0);
  and and_24 (and_24_out, Q3, Q2, not_3_out, not_4_out);
  and and_25 (and_25_out, not_2_out, Q1, not_6_out);
  and and_26 (and_26_out, not_1_out, not_4_out, a);
  or or_1 (newQ3, and_1_out, and_2_out, and_3_out, and_4_out, and_5_out);
  or or_2 (newQ2, and_6_out, and_7_out, and_8_out, and_9_out, and_10_out);
  or or_3 (newQ1, and_11_out, and_12_out, and_13_out, and_14_out, and_15_out, and_16_out, and_17_out);
  or or_4 (newQ0, and_18_out, and_19_out, and_20_out, and_21_out, and_22_out, and_23_out, and_24_out, and_25_out, and_26_out);

  // Notes on the sheet:
  //   Функции возбуждения newQ3..newQ0 по МДНФ (проверочная подсхема)
endmodule
