// Logisim project demux.circ as structural Verilog: 1 circuit, main circuit demux_1_4
module demux_1_4 (
  input  D,
  input  A0,
  input  A1,
  output Y0,
  output Y1,
  output Y2,
  output Y3
);

  Demultiplexer #(.select(2), .enable("false")) demultiplexer_1 (
    .out0(Y0), .out1(Y1), .out2(Y2), .out3(Y3), .in(D), .sel({A1, A0}));
  LED u_Y0 (.in(Y0));
  LED u_Y1 (.in(Y1));
  LED u_Y2 (.in(Y2));
  LED u_Y3 (.in(Y3));

  // Other names for the same wires on the sheet: SEL[1:0] = {A1, A0}

  // Notes on the sheet:
  //   Демультиплексор 1→4: вход D по адресу A1A0 попадает на выход Y<номер>
endmodule
