// Logisim project t.circ as structural Verilog: 1 circuit, main circuit t_trigger
module t_trigger (
  input  T,
  output Q,
  output nQ
);

  wire CLK;

  Clock u_CLK (.out(CLK));
  T_Flip_Flop t_ff_1 (.clk(CLK), .T(T), .Q(Q), .Qn(nQ));  // open: preset, reset, en
  LED u_Q (.in(Q));

  // Notes on the sheet:
  //   T-триггер: T — счётный вход, CLK — синхросигнал, Q/¬Q — выходы
endmodule
