// Logisim project pr04_cu.circ as structural Verilog: 2 circuits, main circuit VM
module VM (
  input  SE,
  input  [15:0] \Ввод ,
  output [15:0] \S_шина ,
  output [19:0] \Управляющее_слово 
);

  wire CF, CLK, cyc0, cyc1, cyc2, cyc3, en1, en2, en3, en4, en5, en6, en7, Fq, GEN, q0, q1, q2, q3, q4, q5,
       q6, q7, q8, q9, q10, q11, q12, q13, q14, q15, t0, t1, t2, t3;
  wire [0:0] FR;
  wire [1:0] T;
  wire [3:0] FL, FLAGS;
  wire [11:0] A12;
  wire [15:0] AC, InpR, IR, MDR, MDRIN, OPA, OPB, OutR, PC, RAMOUT;
  wire [15:12] MAR;

  LED u_t0 (.in(t0));
  LED u_q0 (.in(q0));
  LED u_q8 (.in(q8));
  Clock \u_Генератор  (.out(GEN));
  Decoder #(.select(2), .enable("false")) DC_t (.out0(t0), .out1(t1), .out2(t2), .out3(t3), .sel(T));
  LED u_t1 (.in(t1));
  LED u_q1 (.in(q1));
  LED u_q2 (.in(q2));
  LED u_q9 (.in(q9));
  LED u_q10 (.in(q10));
  Counter #(.width(2), .max('h3)) \u_Счётчик_тактов  (.Q(T), .clk(CLK));  // open: load, D, count, carry, clr
  LED u_t2 (.in(t2));
  LED u_t3 (.in(t3));
  LED u_q3 (.in(q3));
  LED u_q4 (.in(q4));
  LED u_q11 (.in(q11));
  LED u_q12 (.in(q12));
  LED C0 (.in(cyc0));
  LED C1 (.in(cyc1));
  LED u_q5 (.in(q5));
  LED u_q6 (.in(q6));
  LED u_q13 (.in(q13));
  LED u_q14 (.in(q14));
  and and_1 (CLK, GEN, SE);
  Decoder #(.select(2), .enable("false")) DC_C (.out0(cyc0), .out1(cyc1), .out2(cyc2), .out3(cyc3), .sel({Fq, FR[0]}));
  LED C2 (.in(cyc2));
  LED u_q7 (.in(q7));
  LED u_q15 (.in(q15));
  D_Flip_Flop F (.clk(CLK), .D(\Управляющее_слово [1]), .Q(Fq));  // open: Qn, preset, en, reset
  D_Flip_Flop R (.clk(CLK), .D(\Управляющее_слово [0]), .Q(FR[0]));  // open: Qn, preset, en, reset
  LED C3 (.in(cyc3));
  ROM #(.addrWidth(8), .dataWidth(20)) \u_ПЗУ_микрокоманд  (
    .addr({IR[15:12], Fq, FR[0], T}), .data(\Управляющее_слово ));  // open: sel
  Decoder #(.select(4), .enable("false")) \DC_КОП  (
    .out0(q0), .out1(q1), .out2(q2), .out3(q3), .out4(q4), .out5(q5), .out6(q6), .out7(q7), .out8(q8),
    .out9(q9), .out10(q10), .out11(q11), .out12(q12), .out13(q13), .out14(q14), .out15(q15), .sel(IR[15:12]));
  Multiplexer #(.select(1), .width(16), .enable("false")) MS_M (
    .in0(\S_шина ), .in1(RAMOUT), .out(MDRIN), .sel(\Управляющее_слово [3]));
  Decoder #(.select(3), .enable("true"), .disabled(0)) DC (
    .out1(en1), .out2(en2), .out3(en3), .out4(en4), .out5(en5), .out6(en6), .out7(en7),
    .sel(\Управляющее_слово [6:4]), .en(\Управляющее_слово [7]));  // open: out0
  Register #(.width(16)) u_OutR (.D(\S_шина ), .en(en1), .Q(OutR), .clk(CLK));  // open: clr
  Register #(.width(16)) u_InpR (.D(\S_шина ), .en(en2), .Q(InpR), .clk(CLK));  // open: clr
  Register #(.width(16)) u_MDR (.D(MDRIN), .en(en3), .Q(MDR), .clk(CLK));  // open: clr
  Register #(.width(16)) u_MAR (.D(\S_шина ), .en(en4), .Q({MAR, A12}), .clk(CLK));  // open: clr
  Register #(.width(16)) u_IR (.D(\S_шина ), .en(en5), .Q(IR), .clk(CLK));  // open: clr
  Register #(.width(16)) u_AC (.D(\S_шина ), .en(en6), .Q(AC), .clk(CLK));  // open: clr
  Register #(.width(16)) u_PC (.D(\S_шина ), .en(en7), .Q(PC), .clk(CLK));  // open: clr
  Multiplexer #(.select(3), .width(16), .enable("false")) MS_A (
    .in0(PC), .in1(AC), .in2(IR), .in3({MAR, A12}), .in4(MDR), .in5(InpR), .in6(OutR), .in7(\Ввод ),
    .out(OPA), .sel(\Управляющее_слово [19:17]));
  Multiplexer #(.select(3), .width(16), .enable("false")) MS_B (
    .in0(PC), .in1(AC), .in2(IR), .in3({MAR, A12}), .in4(MDR), .in5(InpR), .in6(OutR), .in7(\Ввод ),
    .out(OPB), .sel(\Управляющее_слово [16:14]));
  ALU ALU (
    .A(OPA), .B(OPB), .F(\Управляющее_слово [13]), .M(\Управляющее_слово [12]), .S2(\Управляющее_слово [11]),
    .S1(\Управляющее_слово [10]), .S0(\Управляющее_слово [9]), .C0(\Управляющее_слово [8]), .R(\S_шина ),
    .Z(FLAGS[0]), .S(FLAGS[1]), .C(CF), .V(FLAGS[3]));
  ROM #(.addrWidth(12), .dataWidth(16)) \u_Память__ПЗУ  (.addr(A12), .data(RAMOUT));  // open: sel
  Register #(.width(4)) u_Flags (
    .D({FLAGS[3], CF, FLAGS[1:0]}), .en(\Управляющее_слово [7]), .Q(FL), .clk(CLK));  // open: clr

  // Other names for the same wires on the sheet: CW[19:0] = \Управляющее_слово ; RN = \Управляющее_слово [0];
  //   FN = \Управляющее_слово [1]; WR = \Управляющее_слово [2]; MSM = \Управляющее_слово [3];
  //   DC[2:0] = \Управляющее_слово [6:4]; E = \Управляющее_слово [7]; C0 = \Управляющее_слово [8];
  //   S0 = \Управляющее_слово [9]; S1 = \Управляющее_слово [10]; S2 = \Управляющее_слово [11];
  //   M = \Управляющее_слово [12]; F = \Управляющее_слово [13]; MSB[2:0] = \Управляющее_слово [16:14];
  //   MSA[2:0] = \Управляющее_слово [19:17]; Z = FLAGS[0]; SF = FLAGS[1]; FLAGS[2] = CF; VF = FLAGS[3];
  //   IN[15:0] = \Ввод ; OP[3:0] = IR[15:12]; UADDR[7:0] = {IR[15:12], Fq, FR[0], T}; MAR[11:0] = A12;
  //   S[15:0] = \S_шина ; Rq = FR[0]; FR[1] = Fq

  // Notes on the sheet:
  //   схема совпадения
  //   Устройство управления (рис. 4.1)
  //   contents of ПЗУ_микрокоманд (hex, n*v repeats v):
  //   c0 b8 800d0 1f2 1 1 1 2 400c2 ba 800e2 0 3 3 3 0 c0 b8 800d0 1f2 1 1 1 4*2 0 3 3 3 0 c0 b8 800d0 1f2
  //   1 1 1 2 400c2 ba 302e2 0 3 3 3 0 c0 b8 800d0 1f2 1 1 1 2 400c2 ba 305e2 0 3 3 3 0 c0 b8 800d0 1f2 1
  //   1 1 2 400c2 ba 30ce2 0 3 3 3 0 c0 b8 800d0 1f2 1 1 1 2 400c2 ba 308e2 0 3 3 3 0 c0 b8 800d0 1f2 1 1
  //   1 2 400c2 ba 30ae2 0 3 3 3 0 c0 b8 800d0 1f2 1 1 1 2 400c2 ba 80ee2 0 3 3 3 0 c0 b8 800d0 1f2 1 1 1
  //   2 400c2 ba 80ee2 201e0 3 3 3 0 c0 b8 800d0 1f2 1 1 1 2 400c2 ba 801e2 0 3 3 3 0 c0 b8 800d0 1f2 1 1
  //   1 2 400c2 ba 806e2 0 3 3 3 0 c0 b8 800d0 1f2 1 1 1 2 400f2 2 2 0 3 3 3 0 c0 b8 800d0 1f2 1 1 1 2
  //   24ae2 2 2 0 3 3 3 0 c0 b8 800d0 1f2 1 1 1 2 201e2 2 2 0 3 3 3 0 c0 b8 800d0 1f2 1 1 1 2 a00e2 2 2 0
  //   3 3 3 0 c0 b8 800d0 1f2 1 1 1 2 20092 2 2 0 3 3 3 0
  //   Операционное устройство (рис. 3.4) с памятью программы варианта 28
  //   contents of Память__ПЗУ (hex, n*v repeats v):
  //   1547*0 cb65 2020*0 860b bdf1
endmodule

module ALU (
  input  [15:0] A,
  input  [15:0] B,
  input  F,
  input  M,
  input  S2,
  input  S1,
  input  S0,
  input  C0,
  output [15:0] R,
  output Z,
  output S,
  output C,
  output V
);

  wire ARS, CO, SGN_CH, SGN_EQ;
  wire [15:0] AND, ARITH, ASR, BMA, LOG, nA, NAND, nB, NOR, OR, R0, R1, ROL, ROL2, ROR, ROR2, SHL, SHR, XNOR,
       XOR, Y;

  assign nB = ~B;  // NOT_Gate not_1, 16 bits wide
  assign nA = ~A;  // NOT_Gate not_2, 16 bits wide
  Multiplexer #(.select(2), .width(16), .enable("false")) multiplexer_1 (
    .in0({16{1'b0}}), .in1(B), .in2(nB), .in3({16{1'b1}}), .out(Y), .sel({S1, S0}));
  Adder #(.width(16)) adder_1 (.a(A), .b(Y), .out(ARITH), .cin(C0), .cout(CO));
  Adder #(.width(16)) adder_2 (.a(B), .b(nA), .out(BMA), .cin(C0));  // open: cout
  assign OR = A | B;  // OR_Gate or_1, 16 bits wide
  assign XOR = A ^ B;  // XOR_Gate xor_1, 16 bits wide
  assign AND = A & B;  // AND_Gate and_1, 16 bits wide
  assign NAND = ~(A & B);  // NAND_Gate nand_1, 16 bits wide
  assign NOR = ~(A | B);  // NOR_Gate nor_1, 16 bits wide
  assign XNOR = ~(A ^ B);  // XNOR_Gate xnor_1, 16 bits wide
  Multiplexer #(.select(2), .width(16), .enable("false")) multiplexer_2 (
    .in0(OR), .in1(XOR), .in2(AND), .in3(nA), .out(LOG), .sel({S1, S0}));
  Shifter #(.width(16), .shift("ll")) shifter_1 (.in(A), .\dist (4'b0001), .out(SHL));
  Shifter #(.width(16), .shift("lr")) shifter_2 (.in(A), .\dist (4'b0001), .out(SHR));
  Shifter #(.width(16), .shift("rl")) shifter_3 (.in(A), .\dist (4'b0001), .out(ROL));
  Shifter #(.width(16), .shift("rr")) shifter_4 (.in(A), .\dist (4'b0001), .out(ROR));
  Shifter #(.width(16), .shift("ar")) shifter_5 (.in(A), .\dist (4'b0001), .out(ASR));
  Shifter #(.width(16), .shift("rl")) shifter_6 (.in(A), .\dist (4'b0010), .out(ROL2));
  Shifter #(.width(16), .shift("rr")) shifter_7 (.in(A), .\dist (4'b0010), .out(ROR2));
  xnor xnor_2 (SGN_EQ, A[15], Y[15]);
  xor xor_2 (SGN_CH, A[15], R[15]);
  Comparator #(.width(16)) comparator_1 (.a(R), .b({16{1'b0}}), .eq(Z));  // open: gt, lt
  Multiplexer #(.select(2), .width(16), .enable("false")) multiplexer_3 (
    .in0(ARITH), .in1(LOG), .in2({16{1'b0}}), .in3({16{1'b0}}), .out(R0), .sel({M, S2}));
  nor nor_2 (ARS, F, M, S2);
  and and_2 (C, CO, ARS);
  and and_3 (V, SGN_EQ, SGN_CH, ARS);
  Multiplexer #(.select(4), .width(16), .enable("false")) multiplexer_4 (
    .in0(BMA), .in1(NAND), .in2(NOR), .in3(XNOR), .in4({16{1'b0}}), .in5({16{1'b0}}), .in6({16{1'b0}}),
    .in7({16{1'b0}}), .in8(SHL), .in9(SHR), .in10(ROL), .in11(ROR), .in12(SHL), .in13(ASR), .in14(ROL2),
    .in15(ROR2), .out(R1), .sel({M, S2, S1, S0}));
  Multiplexer #(.select(1), .width(16), .enable("false")) multiplexer_5 (.in0(R0), .in1(R1), .out(R), .sel(F));

  assign S = R[15];

  // Other names for the same wires on the sheet: MS210[3:0] = {M, S2, S1, S0}; S10[1:0] = {S1, S0};
  //   MS2[1:0] = {M, S2}; SF = R[15]

  // Notes on the sheet:
  //   АЛУ 16 разрядов (табл. 3.1): код F M S2 S1 S0 C0
endmodule
