// Logisim project riscv_decoder.circ as structural Verilog: 1 circuit, main circuit riscv_decoder
module riscv_decoder (
  input  [2:0] sel,
  input  [31:0] rs1_val,
  output [6:0] opcode,
  output [4:0] rd,
  output [2:0] funct3,
  output [4:0] rs1,
  output [4:0] rs2,
  output [6:0] funct7,
  output [11:0] imm12,
  output is_addi,
  output [31:0] result
);

  wire comparator_1_eq, comparator_2_eq;
  wire [31:0] bit_extender_1_out;

  Multiplexer #(.select(3), .width(32)) multiplexer_1 (
    .in0(32'h100513), .in1(32'h1597), .in2(32'h1858593), .in3(32'h2800613), .in4(32'h4000893), .in5(32'h73),
    .in6(32'hfe9ff06f), .in7(32'h5d00893), .out({funct7, imm12[4:0], rs1, funct3, rd, opcode}), .sel(sel));  // open: en
  // Probe on {funct7, imm12[4:0], rs1, funct3, rd, opcode}
  assign bit_extender_1_out = {{20{funct7[6]}}, {funct7, imm12[4:0]}};  // Bit_Extender bit_extender_1
  Comparator #(.width(7), .mode("unsigned")) comparator_1 (
    .a(opcode), .b(7'b0010011), .eq(comparator_1_eq));  // open: gt, lt
  Comparator #(.width(3), .mode("unsigned")) comparator_2 (
    .a(funct3), .b(3'b000), .eq(comparator_2_eq));  // open: gt, lt
  // Probe on rs1_val
  and and_1 (is_addi, comparator_1_eq, comparator_2_eq);
  Adder #(.width(32)) adder_1 (.a(bit_extender_1_out), .b(rs1_val), .out(result));  // open: cin, cout
  // Probe on result
  // Probe on bit_extender_1_out

  assign imm12[11:5] = funct7;
  assign rs2 = imm12[4:0];

  // Notes on the sheet:
  //   Память программы: машинные коды из objdump
  //   0:  100e8  li a0,1  (addi a0,x0,1)
  //   1:  100ec  auipc a1,0x1
  //   2:  100f0  addi a1,a1,24
  //   3:  100f4  li a2,40  (addi a2,x0,40)
  //   4:  100f8  li a7,64  (addi a7,x0,64)
  //   5:  100fc  ecall
  //   6:  10100  j main_app  (jal x0,-24)
  //   7:  10104  li a7,93  (hello_world, exit)
  //   ← номер инструкции (0–7)
  //   Дешифратор полей инструкции RISC-V и сумматор для addi
  //   Практическая работа 8, вариант 28 (Мирзоян А.О., ИКБО-41-25)
  //   Исполнение addi:  is_addi = (opcode = 0010011) ∧ (funct3 = 000),  result = rs1_val + sext(imm)
  //   OP-IMM = 0x13
  //   ADDI: funct3 = 000
  //   sext 12→32
  //   Поля инструкции
  //   opcode = instr[6:0]  (тип/класс команды)
  //   rd = instr[11:7]  (регистр-приёмник)
  //   funct3 = instr[14:12]
  //   rs1 = instr[19:15]  (1-й источник)
  //   rs2 = instr[24:20]  (2-й источник, R/S/B)
  //   funct7 = instr[31:25]
  //   imm[11:0] = instr[31:20]  (I-тип)
endmodule
