// Logisim project toupper.circ as structural Verilog: 1 circuit, main circuit toupper
module toupper (
  input  [7:0] c,
  output is_lower,
  output [7:0] out
);

  wire comparator_1_lt, comparator_2_gt;
  wire [7:0] subtractor_1_out;

  // Probe on c
  Comparator #(.width(8), .mode("twosComplement")) comparator_1 (
    .a(c), .b(8'h61), .lt(comparator_1_lt));  // open: gt, eq
  Comparator #(.width(8), .mode("twosComplement")) comparator_2 (
    .a(c), .b(8'h7a), .gt(comparator_2_gt));  // open: eq, lt
  Subtractor #(.width(8)) subtractor_1 (.a(c), .b(8'h20), .out(subtractor_1_out));  // open: bin, bout
  nor nor_1 (is_lower, comparator_1_lt, comparator_2_gt);
  Multiplexer #(.select(1), .width(8)) multiplexer_1 (
    .in0(c), .in1(subtractor_1_out), .out(out), .sel(is_lower));  // open: en
  // Probe on out

  // Notes on the sheet:
  //   'a' = 0x61
  //   'z' = 0x7A
  //   0x20 = 'a' − 'A'
  //   c<'a'
  //   c>'z'
  //   Аппаратный аналог mytoupper: перевод символа в верхний регистр
  //   Практическая работа 9, вариант 28 (Мирзоян А.О., ИКБО-41-25)
  //   c (без изменений)
  //   c − 0x20
  //   Сравнение знаковое (как lb + blt/bgt в листинге 9.8): байты UTF-8 кириллицы
  //   (0xD0, 0xD1, 0x80..0xBF) отрицательны, меньше 'a' и проходят без изменений
  //   0: c,  1: c − 0x20
  //   1 – строчная латинская буква
endmodule
