// Logisim project pr10_replspace.circ as structural Verilog: 2 circuits, main circuit repl_branch
module repl_branch (
  input  [7:0] c,
  output [7:0] out
);

  wire ISSP;

  // Probe on c
  Comparator #(.width(8), .mode("unsigned")) comparator_1 (.a(c), .b(8'h20), .eq(ISSP));  // open: gt, lt
  LED is_space (.in(ISSP));
  Multiplexer #(.select(1), .width(8), .enable("false")) multiplexer_1 (.in0(c), .in1(8'h5f), .out(out), .sel(ISSP));
  // Probe on out

  // Notes on the sheet:
  //   repl с ветвлением: if c == 0x20 then '_' (0x5F) else c (вариант 28)
endmodule

module repl_nobranch (
  input  [7:0] c,
  output [7:0] out
);

  wire ISSP;
  wire [7:0] MASK, MASKF;

  // Probe on c
  Comparator #(.width(8), .mode("unsigned")) comparator_1 (.a(c), .b(8'h20), .eq(ISSP));  // open: gt, lt
  LED is_space (.in(ISSP));
  assign MASKF = {{7{ISSP}}, ISSP};  // Bit_Extender bit_extender_1
  assign MASK = MASKF & 8'h3f;  // AND_Gate and_1, 8 bits wide
  Adder #(.width(8)) adder_1 (.a(c), .b(MASK), .out(out));  // open: cin, cout
  // Probe on out

  // Notes on the sheet:
  //   repl без ветвления: out = c + (is_space·0x3F), 0x20 + 0x3F = 0x5F (вариант 28)
endmodule
