// Logisim project pr10_tolower.circ as structural Verilog: 2 circuits, main circuit tolower_branch
module tolower_branch (
  input  [7:0] c,
  output [7:0] out
);

  wire GE, GE_EQ, GE_GT, LE, LE_EQ, LE_LT, UP;
  wire [7:0] CLOW;

  // Probe on c
  Comparator #(.width(8), .mode("unsigned")) comparator_1 (.a(c), .b(8'h41), .gt(GE_GT), .eq(GE_EQ));  // open: lt
  Comparator #(.width(8), .mode("unsigned")) comparator_2 (.a(c), .b(8'h5a), .eq(LE_EQ), .lt(LE_LT));  // open: gt
  or or_1 (GE, GE_GT, GE_EQ);
  or or_2 (LE, LE_LT, LE_EQ);
  and and_1 (UP, GE, LE);
  LED is_upper (.in(UP));
  Adder #(.width(8)) adder_1 (.a(c), .b(8'h20), .out(CLOW));  // open: cin, cout
  Multiplexer #(.select(1), .width(8), .enable("false")) multiplexer_1 (.in0(c), .in1(CLOW), .out(out), .sel(UP));
  // Probe on out

  // Notes on the sheet:
  //   tolower с ветвлением: if 'A' ≤ c ≤ 'Z' then c + 0x20 else c (вариант 14)
endmodule

module tolower_nobranch (
  input  [7:0] c,
  output [7:0] out
);

  wire GE, GE_EQ, GE_GT, LE, LE_EQ, LE_LT, UP;
  wire [7:0] MASK, MASKX;

  // Probe on c
  Comparator #(.width(8), .mode("unsigned")) comparator_1 (.a(c), .b(8'h41), .gt(GE_GT), .eq(GE_EQ));  // open: lt
  Comparator #(.width(8), .mode("unsigned")) comparator_2 (.a(c), .b(8'h5a), .eq(LE_EQ), .lt(LE_LT));  // open: gt
  or or_1 (GE, GE_GT, GE_EQ);
  or or_2 (LE, LE_LT, LE_EQ);
  and and_1 (UP, GE, LE);
  LED is_upper (.in(UP));
  assign MASKX = {{7{1'b0}}, UP};  // Bit_Extender bit_extender_1
  Shifter #(.width(8), .shift("ll")) shifter_1 (.in(MASKX), .\dist (3'b101), .out(MASK));
  assign out = c | MASK;  // OR_Gate or_3, 8 bits wide
  // Probe on out

  // Notes on the sheet:
  //   tolower без ветвления: out = c | (is_upper << 5) (вариант 14)
endmodule
