// Logisim project practice_3.circ as structural Verilog: 1 circuit, main circuit OU
module OU (
  input  [17:0] CW,
  input  LOAD,
  input  CLK,
  input  [7:0] OUTR_IN,
  input  [7:0] IR_IN,
  output [7:0] MDR_Q
);

  wire ALU_OK, CTRL_OK, DC_MDR, FROM_ALU, READY, RUN, WRITE_MDR;
  wire [7:0] adder_1_out, IR_q, multiplexer_1_out, multiplexer_2_out, multiplexer_3_out, OUTR_q, undriven,
       undriven_2, undriven_3, undriven_4, undriven_5, undriven_6, undriven_7, undriven_8, undriven_9,
       undriven_10, undriven_11, undriven_12;

  not not_1 (RUN, LOAD);
  not not_2 (FROM_ALU, CW[1]);
  Register #(.width(8)) OUTR (.D(OUTR_IN), .en(LOAD), .Q(OUTR_q), .clk(CLK), .clr(1'b0));
  Register #(.width(8)) IR (.D(IR_IN), .en(LOAD), .Q(IR_q), .clk(CLK), .clr(1'b0));
  Comparator #(.width(6), .mode("unsigned")) comparator_1 (.a(CW[11:6]), .b(6'b000011), .eq(ALU_OK));  // open: gt, lt
  Multiplexer #(.width(8), .select(3), .enable("false")) multiplexer_1 (
    .in0(undriven), .in1(undriven_2), .in2(undriven_3), .in3(undriven_4), .in4(undriven_5), .in5(undriven_6),
    .in6(OUTR_q), .in7({8{1'b0}}), .out(multiplexer_1_out), .sel(CW[17:15]));
  Multiplexer #(.width(8), .select(3), .enable("false")) multiplexer_2 (
    .in0(undriven_7), .in1(undriven_8), .in2(IR_q), .in3(undriven_9), .in4(undriven_10), .in5(undriven_11),
    .in6(undriven_12), .in7({8{1'b0}}), .out(multiplexer_2_out), .sel(CW[14:12]));
  and and_1 (CTRL_OK, ALU_OK, RUN);
  Adder #(.width(8)) adder_1 (
    .a(multiplexer_1_out), .b(multiplexer_2_out), .out(adder_1_out), .cin(1'b1));  // open: cout
  Decoder #(.select(3), .enable("true"), .disabled(0)) decoder_1 (
    .out4(DC_MDR), .sel(CW[4:2]), .en(CW[5]));  // open: out0, out1, out2, out3, out5, out6, out7
  Multiplexer #(.width(8), .select(1), .enable("false")) multiplexer_3 (
    .in0(adder_1_out), .in1({8{1'b0}}), .out(multiplexer_3_out), .sel(CW[1]));
  and and_2 (READY, DC_MDR, CTRL_OK);
  and and_3 (WRITE_MDR, READY, FROM_ALU);
  Register #(.width(8)) MDR (.D(multiplexer_3_out), .en(WRITE_MDR), .Q(MDR_Q), .clk(CLK), .clr(1'b0));

  // Other names for the same wires on the sheet: WR = CW[0]; MS_M = CW[1]; DC[3:0] = CW[5:2]; DC_ADDR[2:0] = CW[4:2];
  //   DC_E = CW[5]; ALU_CTRL[5:0] = CW[11:6]; MS_B[2:0] = CW[14:12]; MS_A[2:0] = CW[17:15]

  // Notes on the sheet:
  //   CW: initial=0x320f0
  //   OUTR_IN: initial=0x5
  //   IR_IN: initial=0x3
  //   Вариант 22: MDR ← OUTR + IR + 1
  //   Управляющее слово: MS(A) | MS(B) | ALU | DC | MS(M) | WR
  //   110 | 010 | 000011 | 1100 | 0 | 0 = 110010000011110000
  //   LOAD=1: загрузить OUTR и IR. LOAD=0: выполнить вариант.
  //   CLK 0→1 записывает результат в MDR. WR=0: записи в память нет.
  //   Показ: OUTR_IN=05, IR_IN=03; LOAD=1, CLK 0→1→0; LOAD=0, CLK 0→1. MDR_Q=09.
  //   ALU = 000011
  //   MS(A) = 110
  //   MS(B) = 010
  //   CW = 320F0 (HEX). Данные: 8 бит, HEX.
  //   A + B + 1
  //   DC = 1100: E=1, адрес 100 → MDR
  //   MS(M)=0
endmodule
