// Logisim project пт первая практика — копия.circ as structural Verilog: 1 circuit, main circuit main
module main (
  input  a,
  input  b,
  output c
);

  wire transistor_4_out;

  Transistor transistor_1 (.in(1'b1), .out(c), .gate(a));
  Transistor transistor_2 (.in(1'b1), .out(c), .gate(b));
  Transistor #(.\type ("n")) transistor_3 (.in(transistor_4_out), .out(c), .gate(a));
  Transistor #(.\type ("n")) transistor_4 (.in(1'b0), .out(transistor_4_out), .gate(b));
endmodule
